# Fritzing sketch nRF8001Example (saved by Fritzing 0.9.0b)
breadboards: 1

parts:
  RF1 = nRF8001 Bluetooth LE Breakout
  Part1 = Arduino Uno (Rev3) - ICSP
  LED1 = smd LED [color="Red (633nm)" package="1206 [SMD]"]
  S1 = Pushbutton [package="[SMD]"]
  R1 = Resistor [package="2010 [SMD]"]

nets:
  N1: RF1.SCK, Part1.ICSP_SCK, Part1.D13/SCK
  N2: RF1.MISO, Part1.ICSP_MISO, Part1.D12/MISO
  N3: RF1.MOSI, Part1.ICSP_MOSI, Part1.D11_PWM/MOSI
  N4: RF1.REQ, Part1.D9_PWM
  N5: RF1.RDY, Part1.D8
  GND: RF1.GND, Part1.GND, LED1.cathode, R1.Pin_0
  VIN: RF1.VIN, Part1.5V, S1.Pin_1, S1.Pin_2
  N6: Part1.D6_PWM, LED1.anode
  N7: Part1.D7, S1.Pin_3, S1.Pin_4, R1.Pin_1

custom parts:
  nRF8001 Bluetooth LE Breakout: nRF8001 Breakout Board
